// Logisim project oblig2.circ as structural Verilog: 1 circuit, main circuit main
module main (
);

  wire [11:0] _1_out;

  Button _1 (.out(_1_out[0]));
  Button _4 (.out(_1_out[3]));
  Button _7 (.out(_1_out[6]));
  Button button (.out(_1_out[9]));
  Button _2 (.out(_1_out[1]));
  Button _5 (.out(_1_out[4]));
  Button _8 (.out(_1_out[7]));
  Button _0 (.out(_1_out[10]));
  Button _3 (.out(_1_out[2]));
  Button _6 (.out(_1_out[5]));
  Button _9 (.out(_1_out[8]));
  Button button_2 (.out(_1_out[11]));
  LED led_1 ();  // open: in
endmodule
